# Fritzing sketch Fritzing Diagram (saved by Fritzing 0.9.3b)
breadboards: 1

parts:
  Componente1 = Pro Trinket 5V
  RF1 = nRF8001 Bluetooth LE Breakout
  U1 = LIPO-110mAh [package=lipo-110]  # not connected

nets:
  GND: Componente1.GND, RF1.GND
  +5V: Componente1.+5V, RF1.VIN
  N1: Componente1.TXD, RF1.RDY
  N2: Componente1.D9, RF1.RST
  N3: Componente1.D10, RF1.REQ
  N4: Componente1.D11, RF1.MOSI
  N5: Componente1.D12, RF1.MISO
  N6: Componente1.D13, RF1.SCK

custom parts:
  Pro Trinket 5V: The Pro Trinket 5V is like an Arduino Pro Mini with more pins and USB included. Built with the common core Arduino chip, the ATmega328p, it has 18 GPIO, 2 extra analog inputs, 28K of flash, and 2K of RAM. It has onboard USB bootloading support with Optiboot support, so you can either program your Pro Trinket over USB or with a FTDI cable. The Pro Trinket is programmable using the Arduino IDE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
  nRF8001 Bluetooth LE Breakout: nRF8001 Breakout Board
